# Fritzing sketch waterbot (saved by Fritzing 0.9.3b)
circuit board: 4.35588cm x 3.50614cm
breadboards: 1

parts:
  C1 = Ceramic Capacitor [capacitance=0.1µF package="100 mil [THT, multilayer]"]
  R1 = Resistor [tolerance=±5% resistance=10k package=THT]
  Meter = Screw terminal - 2 pins [package=THT]
  Photon = Photon

nets:
  N1: C1.0, R1.Pin_0, Meter.pin2, Photon.WKP, Photon.D2
  N2: C1.1, Meter.pin1, Photon.3V3
  N3: R1.Pin_1, Photon.GND, Photon.VBAT

notes:
  Connect VBAT to GND (blue wire) only if not using battery
  Connect VBAT to GND only if not using battery
